// Digital circuit 1-bit-comparator.dig as structural Verilog
module _1_bit_comparator (
  input  A,
  input  B,
  output EQ
);

  wire xor_1_out;

  xor xor_1 (xor_1_out, A, B);
  not not_1 (EQ, xor_1_out);
endmodule
