// Digital circuit 1-bit-full-adder.dig as structural Verilog
module _1_bit_full_adder (
  input  cin,
  input  a,
  input  b,
  output sum,
  output cout
);

  wire and_1_out, and_2_out, and_3_out, and_4_out, and_5_out, and_6_out, and_7_out, and_8_out;

  and and_1 (and_1_out, ~a, ~b, cin);  // And
  and and_2 (and_2_out, ~a, b, ~cin);  // And
  and and_3 (and_3_out, a, ~b, ~cin);  // And
  and and_4 (and_4_out, a, b, cin);
  and and_5 (and_5_out, ~a, b, cin);  // And
  and and_6 (and_6_out, a, ~b, cin);  // And
  and and_7 (and_7_out, a, b, ~cin);  // And
  and and_8 (and_8_out, a, b, cin);
  or or_1 (sum, and_1_out, and_2_out, and_3_out, and_4_out);
  or or_2 (cout, and_5_out, and_6_out, and_7_out, and_8_out);
endmodule
