// Digital circuit 2_to_4_decoder.dig as structural Verilog
module _2_to_4_decoder (
  input  [1:0] SEL,
  output r0,
  output r1,
  output r2,
  output r3
);

  and and_1 (r0, ~SEL[0], ~SEL[1]);  // And
  and and_2 (r1, SEL[0], ~SEL[1]);  // And
  and and_3 (r2, ~SEL[0], SEL[1]);  // And
  and and_4 (r3, SEL[0], SEL[1]);
endmodule
