// Digital circuit 32-bit-comparator.dig as structural Verilog
module _32_bit_comparator (
  input  [31:0] A,
  input  [31:0] B,
  output EQ
);

  wire _8_bit_comparator_1_eq, _8_bit_comparator_2_eq, _8_bit_comparator_3_eq, _8_bit_comparator_4_eq;

  _8_bit_comparator _8_bit_comparator_1 (.A(A[7:0]), .B(B[7:0]), .EQ(_8_bit_comparator_1_eq));
  _8_bit_comparator _8_bit_comparator_2 (.A(A[15:8]), .B(B[15:8]), .EQ(_8_bit_comparator_2_eq));
  _8_bit_comparator _8_bit_comparator_3 (.A(A[23:16]), .B(B[23:16]), .EQ(_8_bit_comparator_3_eq));
  _8_bit_comparator _8_bit_comparator_4 (.A(A[31:24]), .B(B[31:24]), .EQ(_8_bit_comparator_4_eq));
  and and_1 (EQ, _8_bit_comparator_1_eq, _8_bit_comparator_2_eq, _8_bit_comparator_3_eq, _8_bit_comparator_4_eq);
endmodule
