// Digital circuit 4-bit-comparator.dig as structural Verilog
module _4_bit_comparator (
  input  [3:0] A,
  input  [3:0] B,
  output EQ
);

  wire _1_bit_comparator_1_eq, _1_bit_comparator_2_eq, _1_bit_comparator_3_eq, _1_bit_comparator_4_eq;

  _1_bit_comparator _1_bit_comparator_1 (.A(A[0]), .B(B[0]), .EQ(_1_bit_comparator_1_eq));
  _1_bit_comparator _1_bit_comparator_2 (.A(A[1]), .B(B[1]), .EQ(_1_bit_comparator_2_eq));
  _1_bit_comparator _1_bit_comparator_3 (.A(A[2]), .B(B[2]), .EQ(_1_bit_comparator_3_eq));
  _1_bit_comparator _1_bit_comparator_4 (.A(A[3]), .B(B[3]), .EQ(_1_bit_comparator_4_eq));
  and and_1 (EQ, _1_bit_comparator_1_eq, _1_bit_comparator_2_eq, _1_bit_comparator_3_eq, _1_bit_comparator_4_eq);
endmodule
