// Digital circuit 8-bit-comparator.dig as structural Verilog
module _8_bit_comparator (
  input  [7:0] A,
  input  [7:0] B,
  output EQ
);

  wire _4_bit_comparator_1_eq, _4_bit_comparator_2_eq;

  _4_bit_comparator _4_bit_comparator_1 (.A(A[3:0]), .B(B[3:0]), .EQ(_4_bit_comparator_1_eq));
  _4_bit_comparator _4_bit_comparator_2 (.A(A[7:4]), .B(B[7:4]), .EQ(_4_bit_comparator_2_eq));
  and and_1 (EQ, _4_bit_comparator_1_eq, _4_bit_comparator_2_eq);
endmodule
