// Digital circuit 8-bit-counter.dig as structural Verilog
module _8_bit_counter (
  input  CLK,
  input  CLR,
  output [7:0] COUNT
);

  wire [7:0] _8_bit_ripple_carry_adder_1_sum;

  _8_bit_register _8_bit_register_1 (.D(_8_bit_ripple_carry_adder_1_sum), .CLK(CLK), .EN(1'b1), .CLR(CLR), .Q(COUNT));
  _8_bit_ripple_carry_adder _8_bit_ripple_carry_adder_1 (
    .cin(1'b0), .a(COUNT), .b(8'h1), .sum(_8_bit_ripple_carry_adder_1_sum));  // open: cout
endmodule
