// Digital circuit 8-bit-register.dig as structural Verilog
module _8_bit_register (
  input  [7:0] D,
  input  CLK,
  input  EN,
  input  CLR,
  output [7:0] Q
);

  d_flip_flop d_flip_flop_1 (.D(D[0]), .CLK(CLK), .EN(EN), .CLR(CLR), .Q(Q[0]));  // open: nQ
  d_flip_flop d_flip_flop_2 (.D(D[1]), .CLK(CLK), .EN(EN), .CLR(CLR), .Q(Q[1]));  // open: nQ
  d_flip_flop d_flip_flop_3 (.D(D[2]), .CLK(CLK), .EN(EN), .CLR(CLR), .Q(Q[2]));  // open: nQ
  d_flip_flop d_flip_flop_4 (.D(D[3]), .CLK(CLK), .EN(EN), .CLR(CLR), .Q(Q[3]));  // open: nQ
  d_flip_flop d_flip_flop_5 (.D(D[4]), .CLK(CLK), .EN(EN), .CLR(CLR), .Q(Q[4]));  // open: nQ
  d_flip_flop d_flip_flop_6 (.D(D[5]), .CLK(CLK), .EN(EN), .CLR(CLR), .Q(Q[5]));  // open: nQ
  d_flip_flop d_flip_flop_7 (.D(D[6]), .CLK(CLK), .EN(EN), .CLR(CLR), .Q(Q[6]));  // open: nQ
  d_flip_flop d_flip_flop_8 (.D(D[7]), .CLK(CLK), .EN(EN), .CLR(CLR), .Q(Q[7]));  // open: nQ
endmodule
