// Digital circuit 8-bit-ripple-carry-adder.dig as structural Verilog
module _8_bit_ripple_carry_adder (
  input  cin,
  input  [7:0] a,
  input  [7:0] b,
  output cout,
  output [7:0] sum
);

  wire _1_bit_full_adder_1_cout, _1_bit_full_adder_2_cout, _1_bit_full_adder_3_cout,
       _1_bit_full_adder_4_cout, _1_bit_full_adder_5_cout, _1_bit_full_adder_6_cout, _1_bit_full_adder_7_cout;

  _1_bit_full_adder _1_bit_full_adder_1 (.cin(cin), .a(a[0]), .b(b[0]), .sum(sum[0]), .cout(_1_bit_full_adder_1_cout));
  _1_bit_full_adder _1_bit_full_adder_2 (
    .cin(_1_bit_full_adder_1_cout), .a(a[1]), .b(b[1]), .sum(sum[1]), .cout(_1_bit_full_adder_2_cout));
  _1_bit_full_adder _1_bit_full_adder_3 (
    .cin(_1_bit_full_adder_2_cout), .a(a[2]), .b(b[2]), .sum(sum[2]), .cout(_1_bit_full_adder_3_cout));
  _1_bit_full_adder _1_bit_full_adder_4 (
    .cin(_1_bit_full_adder_3_cout), .a(a[3]), .b(b[3]), .sum(sum[3]), .cout(_1_bit_full_adder_4_cout));
  _1_bit_full_adder _1_bit_full_adder_5 (
    .cin(_1_bit_full_adder_4_cout), .a(a[4]), .b(b[4]), .sum(sum[4]), .cout(_1_bit_full_adder_5_cout));
  _1_bit_full_adder _1_bit_full_adder_6 (
    .cin(_1_bit_full_adder_5_cout), .a(a[5]), .b(b[5]), .sum(sum[5]), .cout(_1_bit_full_adder_6_cout));
  _1_bit_full_adder _1_bit_full_adder_7 (
    .cin(_1_bit_full_adder_6_cout), .a(a[6]), .b(b[6]), .sum(sum[6]), .cout(_1_bit_full_adder_7_cout));
  _1_bit_full_adder _1_bit_full_adder_8 (.cin(_1_bit_full_adder_7_cout), .a(a[7]), .b(b[7]), .sum(sum[7]), .cout(cout));
endmodule
