// Digital circuit analyze_decode.dig as structural Verilog
module analyze_decode (
  input  [31:0] IW,
  output [2:0] inum
);

  wire and_1_out, b_type_eq, I_type_eq, j_eq, jal_eq, jalr_eq, load_eq, r_type_eq, s_type_eq;

  _7_bit_comparator I_type (.A(IW[6:0]), .B(7'b0010011), .EQ(I_type_eq));
  _7_bit_comparator r_type (.A(IW[6:0]), .B(7'b0110011), .EQ(r_type_eq));
  _7_bit_comparator load (.A(IW[6:0]), .B(7'b0000011), .EQ(load_eq));
  _7_bit_comparator s_type (.A(IW[6:0]), .B(7'b0100011), .EQ(s_type_eq));
  _7_bit_comparator b_type (.A(IW[6:0]), .B(7'b1100011), .EQ(b_type_eq));
  _7_bit_comparator jal (.A(IW[6:0]), .B(7'b1101111), .EQ(jal_eq));
  _5_bit_comparator j (.A({5{1'b0}}), .B(IW[11:7]), .EQ(j_eq));
  _7_bit_comparator jalr (.A(IW[6:0]), .B(7'b1100111), .EQ(jalr_eq));
  and and_1 (and_1_out, jal_eq, j_eq);
  PriorityEncoder #(.Selector_Bits(3)) priorityencoder_1 (
    .in0(I_type_eq), .in1(r_type_eq), .in2(load_eq), .in3(s_type_eq), .in4(b_type_eq), .in5(jal_eq),
    .in6(and_1_out), .in7(jalr_eq), .num(inum));  // open: any
endmodule
