// Digital circuit d-flip-flop.dig as structural Verilog
module d_flip_flop (
  input  D,
  input  CLK,
  input  EN,
  input  CLR,
  output Q,
  output nQ
);

  wire d_latch_1_q, multiplexer_1_out, not_1_out;

  // Probe on D
  // Probe on CLK
  Multiplexer multiplexer_1 (.sel(EN), .in_0(Q), .in_1(D), .out(multiplexer_1_out));
  not not_1 (not_1_out, CLK);
  d_latch d_latch_1 (.C(not_1_out), .D(multiplexer_1_out), .CLR(CLR), .Q(d_latch_1_q));  // open: nQ
  d_latch d_latch_2 (.C(CLK), .D(d_latch_1_q), .CLR(CLR), .Q(Q), .nQ(nQ));
  // Probe on Q
  // Probe on nQ
endmodule
