// Digital circuit d-latch.dig as structural Verilog
module d_latch (
  input  C,
  input  D,
  input  CLR,
  output Q,
  output nQ
);

  wire and_1_out, and_2_out, and_3_out, or_1_out;

  or or_1 (or_1_out, C, CLR);
  and and_1 (and_1_out, D, ~CLR);  // And
  and and_2 (and_2_out, or_1_out, ~and_1_out);  // And
  and and_3 (and_3_out, or_1_out, and_1_out);
  s_r_latch s_r_latch_1 (.R(and_2_out), .S(and_3_out), .Q(Q), .nQ(nQ));
endmodule
