// Digital circuit project04.dig as structural Verilog
module project04 (
  input  [1:0] PROG,
  input  CLR,
  input  CLK,
  output DONE,
  output [7:0] ITYPE,
  output [7:0] RTYPE,
  output [7:0] LOAD,
  output [7:0] STYPE,
  output [7:0] BTYPE,
  output [7:0] JAL,
  output [7:0] J,
  output [7:0] JALR,
  output [7:0] TOTAL
);

  wire and_1_out, decoder_1_out_0, decoder_1_out_1, decoder_1_out_2, decoder_1_out_3, decoder_1_out_4,
       decoder_1_out_5, decoder_1_out_6, decoder_1_out_7;
  wire [2:0] analyze_decode_1_inum;
  wire [7:0] _8_bit_addr_sum, multiplexer_1_out;
  wire [31:0] instruction_memory_1_d;

  and and_1 (and_1_out, CLK, ~DONE);  // And
  _8_bit_counter _8_bit_counter_1 (.COUNT(TOTAL), .CLK(and_1_out), .CLR(CLR));
  instruction_memory instruction_memory_1 (.A(TOTAL), .D(instruction_memory_1_d), .PN(PROG));
  _32_bit_comparator _32_bit_comparator_1 (.A(instruction_memory_1_d), .B(32'hc0001073), .EQ(DONE));
  analyze_decode analyze_decode_1 (.IW(instruction_memory_1_d), .inum(analyze_decode_1_inum));
  Decoder #(.Selector_Bits(3)) decoder_1 (
    .sel(analyze_decode_1_inum), .out_0(decoder_1_out_0), .out_1(decoder_1_out_1), .out_2(decoder_1_out_2),
    .out_3(decoder_1_out_3), .out_4(decoder_1_out_4), .out_5(decoder_1_out_5), .out_6(decoder_1_out_6),
    .out_7(decoder_1_out_7));
  _8_bit_ripple_carry_adder _8_bit_addr (
    .cin(1'b0), .a(8'h1), .b(multiplexer_1_out), .sum(_8_bit_addr_sum));  // open: cout
  _8_bit_register _8_bit_register_1 (.D(_8_bit_addr_sum), .CLK(and_1_out), .EN(decoder_1_out_0), .CLR(CLR), .Q(ITYPE));
  _8_bit_register _8_bit_register_2 (.D(_8_bit_addr_sum), .CLK(and_1_out), .EN(decoder_1_out_1), .CLR(CLR), .Q(RTYPE));
  _8_bit_register _8_bit_register_3 (.D(_8_bit_addr_sum), .CLK(and_1_out), .EN(decoder_1_out_2), .CLR(CLR), .Q(LOAD));
  _8_bit_register _8_bit_register_4 (.D(_8_bit_addr_sum), .CLK(and_1_out), .EN(decoder_1_out_3), .CLR(CLR), .Q(STYPE));
  _8_bit_register _8_bit_register_5 (.D(_8_bit_addr_sum), .CLK(and_1_out), .EN(decoder_1_out_4), .CLR(CLR), .Q(BTYPE));
  _8_bit_register _8_bit_register_6 (.D(_8_bit_addr_sum), .CLK(and_1_out), .EN(decoder_1_out_5), .CLR(CLR), .Q(JAL));
  _8_bit_register _8_bit_register_7 (.D(_8_bit_addr_sum), .CLK(and_1_out), .EN(decoder_1_out_6), .CLR(CLR), .Q(J));
  _8_bit_register _8_bit_register_8 (.D(_8_bit_addr_sum), .CLK(and_1_out), .EN(decoder_1_out_7), .CLR(CLR), .Q(JALR));
  Multiplexer #(.Bits(8), .Selector_Bits(3)) multiplexer_1 (
    .sel(analyze_decode_1_inum), .in_0(ITYPE), .in_1(RTYPE), .in_2(LOAD), .in_3(STYPE), .in_4(BTYPE),
    .in_5(JAL), .in_6(J), .in_7(JALR), .out(multiplexer_1_out));
endmodule
